// Logisim project ETFStudent.circ as structural Verilog: 13 circuits, main circuit REG32_LD
module REG32_LD (
  input  [31:0] I15__0,
  input  LD,
  input  mr,
  input  CLK,
  output [31:0] A15__0
);

  // REG16_LD reg16_ld_1: pin names not known; wires that end beside it: CLK, mr, I15__0[31:16], A15__0[31:16], LD
  // REG16_LD reg16_ld_2: pin names not known; wires that end beside it: CLK, mr, I15__0[15:0], A15__0[15:0], LD

  // Notes on the sheet:
  //   __
endmodule

module KMADR (
  input  immed,
  input  memdir,
  input  regdir,
  input  regindpom,
  output [3:0] Adr3__0
);

  assign Adr3__0 = immed ? 4'b0010 : 4'bz;  // Controlled_Buffer controlled_buffer_1
  assign Adr3__0 = memdir ? 4'b0100 : 4'bz;  // Controlled_Buffer controlled_buffer_2
  assign Adr3__0 = regdir ? 4'b0101 : 4'bz;  // Controlled_Buffer controlled_buffer_3
  assign Adr3__0 = regindpom ? 4'b0111 : 4'bz;  // Controlled_Buffer controlled_buffer_4
endmodule

module KMOPR (
  input  LD,
  input  ST,
  input  ADD,
  input  SUB,
  input  BLSS,
  input  JLEQ,
  input  JMP,
  input  JSR,
  input  RTS,
  input  RTI,
  input  HALT,
  output [5:0] Adr5__0
);

  assign Adr5__0 = LD ? 6'b000010 : 6'bz;  // Controlled_Buffer controlled_buffer_1
  assign Adr5__0 = ST ? 6'b000100 : 6'bz;  // Controlled_Buffer controlled_buffer_2
  assign Adr5__0 = ADD ? 6'b001010 : 6'bz;  // Controlled_Buffer controlled_buffer_3
  assign Adr5__0 = SUB ? 6'b001100 : 6'bz;  // Controlled_Buffer controlled_buffer_4
  assign Adr5__0 = BLSS ? 6'b001110 : 6'bz;  // Controlled_Buffer controlled_buffer_5
  assign Adr5__0 = JLEQ ? 6'b010000 : 6'bz;  // Controlled_Buffer controlled_buffer_6
  assign Adr5__0 = JMP ? 6'b010001 : 6'bz;  // Controlled_Buffer controlled_buffer_7
  assign Adr5__0 = JSR ? 6'b010010 : 6'bz;  // Controlled_Buffer controlled_buffer_8
  assign Adr5__0 = RTS ? 6'b010111 : 6'bz;  // Controlled_Buffer controlled_buffer_9
  assign Adr5__0 = RTI ? 6'b011110 : 6'bz;  // Controlled_Buffer controlled_buffer_10
  assign Adr5__0 = HALT ? 6'b100010 : 6'bz;  // Controlled_Buffer controlled_buffer_11
endmodule

module REG6_INC_LD (
  input  [5:0] I5__0,
  input  LD,
  input  INC,
  input  mr,
  input  CLK,
  output [5:0] A5__0
);

  wire reg2m_inc_ld_1_p7, reg2m_inc_ld_2_p8;

  // REG2m_INC_LD reg2m_inc_ld_1: pin names not known; wires that end beside it: CLK, mr, I5__0[5:4], A5__0[5:4], LD, INC, reg2m_inc_ld_1_p7
  // REG2m_INC_LD reg2m_inc_ld_2: pin names not known; wires that end beside it: CLK, reg2m_inc_ld_1_p7, mr, I5__0[3:2], A5__0[3:2], LD, INC, reg2m_inc_ld_2_p8
  // REG2m_INC_LD reg2m_inc_ld_3: pin names not known; wires that end beside it: CLK, reg2m_inc_ld_2_p8, mr, I5__0[1:0], A5__0[1:0], LD, INC, INC

  // Notes on the sheet:
  //   __
endmodule

module GPR16x16 (
  input  CLK,
  input  WR,
  input  [15:0] DIN,
  input  [3:0] ADDR,
  output [15:0] DOUT
);

  wire CS0, CS1, CS2, CS3, CS4, CS5, CS6, CS7, CS8, CS9, CS10, CS11, CS12, CS13, CS14, CS15, reg16_ld_1_p4,
       reg16_ld_2_p4, reg16_ld_3_p4, reg16_ld_4_p4, reg16_ld_5_p4, reg16_ld_6_p4, reg16_ld_7_p4,
       reg16_ld_8_p4, reg16_ld_9_p4, reg16_ld_10_p4, reg16_ld_11_p4, reg16_ld_12_p4, reg16_ld_13_p4,
       reg16_ld_14_p4, reg16_ld_15_p4, reg16_ld_16_p4;
  wire [15:0] reg16_ld_1_p3, reg16_ld_2_p3, reg16_ld_3_p3, reg16_ld_4_p3, reg16_ld_5_p3, reg16_ld_6_p3,
       reg16_ld_7_p3, reg16_ld_8_p3, reg16_ld_9_p3, reg16_ld_10_p3, reg16_ld_11_p3, reg16_ld_12_p3,
       reg16_ld_13_p3, reg16_ld_14_p3, reg16_ld_15_p3, reg16_ld_16_p3;

  // NOT_Gate not_1 has open pins: in=ADDR[3], out=open
  // DC3_8 dc3_8_1: pin names not known; wires that end beside it: ADDR[2:0], CS0, CS1, CS2, CS3, CS4, CS5, CS6, CS7
  // DC3_8 dc3_8_2: pin names not known; wires that end beside it: ADDR[2:0], ADDR[3], CS8, CS9, CS10, CS11, CS12, CS13, CS14, CS15
  // REG16_LD reg16_ld_1: pin names not known; wires that end beside it: CLK, DIN, reg16_ld_1_p3, reg16_ld_1_p4
  assign DOUT = CS0 ? reg16_ld_1_p3 : 16'bz;  // Controlled_Buffer controlled_buffer_1
  // REG16_LD reg16_ld_2: pin names not known; wires that end beside it: CLK, DIN, reg16_ld_2_p3, reg16_ld_2_p4
  assign DOUT = CS1 ? reg16_ld_2_p3 : 16'bz;  // Controlled_Buffer controlled_buffer_2
  // REG16_LD reg16_ld_3: pin names not known; wires that end beside it: CLK, DIN, reg16_ld_3_p3, reg16_ld_3_p4
  assign DOUT = CS2 ? reg16_ld_3_p3 : 16'bz;  // Controlled_Buffer controlled_buffer_3
  // REG16_LD reg16_ld_4: pin names not known; wires that end beside it: CLK, DIN, reg16_ld_4_p3, reg16_ld_4_p4
  assign DOUT = CS3 ? reg16_ld_4_p3 : 16'bz;  // Controlled_Buffer controlled_buffer_4
  and and_1 (reg16_ld_1_p4, CS0, WR);
  and and_2 (reg16_ld_2_p4, CS1, WR);
  and and_3 (reg16_ld_3_p4, CS2, WR);
  and and_4 (reg16_ld_4_p4, CS3, WR);
  // REG16_LD reg16_ld_5: pin names not known; wires that end beside it: CLK, DIN, reg16_ld_5_p3, reg16_ld_5_p4
  assign DOUT = CS4 ? reg16_ld_5_p3 : 16'bz;  // Controlled_Buffer controlled_buffer_5
  // REG16_LD reg16_ld_6: pin names not known; wires that end beside it: CLK, DIN, reg16_ld_6_p3, reg16_ld_6_p4
  assign DOUT = CS5 ? reg16_ld_6_p3 : 16'bz;  // Controlled_Buffer controlled_buffer_6
  // REG16_LD reg16_ld_7: pin names not known; wires that end beside it: CLK, DIN, reg16_ld_7_p3, reg16_ld_7_p4
  assign DOUT = CS6 ? reg16_ld_7_p3 : 16'bz;  // Controlled_Buffer controlled_buffer_7
  // REG16_LD reg16_ld_8: pin names not known; wires that end beside it: CLK, DIN, reg16_ld_8_p3, reg16_ld_8_p4
  assign DOUT = CS7 ? reg16_ld_8_p3 : 16'bz;  // Controlled_Buffer controlled_buffer_8
  and and_5 (reg16_ld_5_p4, CS4, WR);
  and and_6 (reg16_ld_6_p4, CS5, WR);
  and and_7 (reg16_ld_7_p4, CS6, WR);
  and and_8 (reg16_ld_8_p4, CS7, WR);
  // REG16_LD reg16_ld_9: pin names not known; wires that end beside it: CLK, DIN, reg16_ld_9_p3, reg16_ld_9_p4
  assign DOUT = CS8 ? reg16_ld_9_p3 : 16'bz;  // Controlled_Buffer controlled_buffer_9
  // REG16_LD reg16_ld_10: pin names not known; wires that end beside it: CLK, DIN, reg16_ld_10_p3, reg16_ld_10_p4
  assign DOUT = CS9 ? reg16_ld_10_p3 : 16'bz;  // Controlled_Buffer controlled_buffer_10
  // REG16_LD reg16_ld_11: pin names not known; wires that end beside it: CLK, DIN, reg16_ld_11_p3, reg16_ld_11_p4
  assign DOUT = CS10 ? reg16_ld_11_p3 : 16'bz;  // Controlled_Buffer controlled_buffer_11
  // REG16_LD reg16_ld_12: pin names not known; wires that end beside it: CLK, DIN, reg16_ld_12_p3, reg16_ld_12_p4
  assign DOUT = CS11 ? reg16_ld_12_p3 : 16'bz;  // Controlled_Buffer controlled_buffer_12
  and and_9 (reg16_ld_9_p4, CS8, WR);
  and and_10 (reg16_ld_10_p4, CS9, WR);
  and and_11 (reg16_ld_11_p4, CS10, WR);
  and and_12 (reg16_ld_12_p4, CS11, WR);
  // REG16_LD reg16_ld_13: pin names not known; wires that end beside it: CLK, DIN, reg16_ld_13_p3, reg16_ld_13_p4
  assign DOUT = CS12 ? reg16_ld_13_p3 : 16'bz;  // Controlled_Buffer controlled_buffer_13
  // REG16_LD reg16_ld_14: pin names not known; wires that end beside it: CLK, DIN, reg16_ld_14_p3, reg16_ld_14_p4
  assign DOUT = CS13 ? reg16_ld_14_p3 : 16'bz;  // Controlled_Buffer controlled_buffer_14
  // REG16_LD reg16_ld_15: pin names not known; wires that end beside it: CLK, DIN, reg16_ld_15_p3, reg16_ld_15_p4
  assign DOUT = CS14 ? reg16_ld_15_p3 : 16'bz;  // Controlled_Buffer controlled_buffer_15
  // REG16_LD reg16_ld_16: pin names not known; wires that end beside it: CLK, DIN, reg16_ld_16_p3, reg16_ld_16_p4
  assign DOUT = CS15 ? reg16_ld_16_p3 : 16'bz;  // Controlled_Buffer controlled_buffer_16
  and and_13 (reg16_ld_13_p4, CS12, WR);
  and and_14 (reg16_ld_14_p4, CS13, WR);
  and and_15 (reg16_ld_15_p4, CS14, WR);
  and and_16 (reg16_ld_16_p4, CS15, WR);

  // Notes on the sheet:
  //   ACC == R[0]
  //   PC == R[2]
  //   SP == R[1]
endmodule

module GPR16x16_ACC_SP_PC (
  input  CLK,
  input  WR,
  input  [15:0] DIN,
  input  [3:0] ADDR,
  input  rst,
  output [15:0] DOUT
);

  wire and_2_out, and_3_out, and_4_out, CS0, CS1, CS2, CS3, CS4, CS5, CS6, CS7, CS8, CS9, CS10, CS11, CS12,
       CS13, CS14, CS15, mp2_16b_1_p3, mp2_16b_2_p3, mp2_16b_3_p3, or_2_out, or_3_out, reg16_ld_1_p4,
       reg16_ld_2_p4, reg16_ld_5_p4, reg16_ld_6_p4, reg16_ld_7_p4, reg16_ld_8_p4, reg16_ld_9_p4,
       reg16_ld_10_p4, reg16_ld_11_p4, reg16_ld_12_p4, reg16_ld_13_p4, reg16_ld_14_p4, reg16_ld_15_p4,
       reg16_ld_16_p4;
  wire [15:0] reg16_ld_1_p3, reg16_ld_2_p3, reg16_ld_3_p3, reg16_ld_4_p3, reg16_ld_5_p3, reg16_ld_6_p3,
       reg16_ld_7_p3, reg16_ld_8_p3, reg16_ld_9_p3, reg16_ld_10_p3, reg16_ld_11_p3, reg16_ld_12_p3,
       reg16_ld_13_p3, reg16_ld_14_p3, reg16_ld_15_p3, reg16_ld_16_p3;

  // REG16_LD reg16_ld_1: pin names not known; wires that end beside it: CLK, DIN, reg16_ld_1_p3, reg16_ld_1_p4
  assign DOUT = CS3 ? reg16_ld_1_p3 : 16'bz;  // Controlled_Buffer controlled_buffer_1
  // NOT_Gate not_1 has open pins: in=ADDR[3], out=open
  // DC3_8 dc3_8_1: pin names not known; wires that end beside it: ADDR[2:0], CS0, CS1, CS2, CS3, CS4, CS5, CS6, CS7
  and and_1 (reg16_ld_1_p4, CS3, WR);
  // DC3_8 dc3_8_2: pin names not known; wires that end beside it: ADDR[2:0], ADDR[3], CS8, CS9, CS10, CS11, CS12, CS13, CS14, CS15
  // MP2_16b mp2_16b_1: pin names not known; wires that end beside it: rst, DIN, mp2_16b_1_p3, {16{1'b0}}, 1'b1
  // REG16_LD reg16_ld_2: pin names not known; wires that end beside it: CLK, mp2_16b_1_p3, reg16_ld_2_p3, reg16_ld_2_p4
  assign DOUT = CS0 ? reg16_ld_2_p3 : 16'bz;  // Controlled_Buffer controlled_buffer_2
  or or_1 (reg16_ld_2_p4, and_2_out, rst);
  // MP2_16b mp2_16b_2: pin names not known; wires that end beside it: rst, DIN, mp2_16b_2_p3, 16'hf000, 1'b1
  or or_2 (or_2_out, and_3_out, rst);
  // REG16_LD reg16_ld_3: pin names not known; wires that end beside it: CLK, mp2_16b_2_p3, reg16_ld_3_p3, or_2_out
  assign DOUT = CS1 ? reg16_ld_3_p3 : 16'bz;  // Controlled_Buffer controlled_buffer_3
  // MP2_16b mp2_16b_3: pin names not known; wires that end beside it: rst, DIN, mp2_16b_3_p3, 16'h1000, 1'b1
  or or_3 (or_3_out, and_4_out, rst);
  // REG16_LD reg16_ld_4: pin names not known; wires that end beside it: CLK, mp2_16b_3_p3, reg16_ld_4_p3, or_3_out
  assign DOUT = CS2 ? reg16_ld_4_p3 : 16'bz;  // Controlled_Buffer controlled_buffer_4
  and and_2 (and_2_out, CS0, WR);
  and and_3 (and_3_out, CS1, WR);
  and and_4 (and_4_out, CS2, WR);
  // REG16_LD reg16_ld_5: pin names not known; wires that end beside it: CLK, DIN, reg16_ld_5_p3, reg16_ld_5_p4
  assign DOUT = CS4 ? reg16_ld_5_p3 : 16'bz;  // Controlled_Buffer controlled_buffer_5
  // REG16_LD reg16_ld_6: pin names not known; wires that end beside it: CLK, DIN, reg16_ld_6_p3, reg16_ld_6_p4
  assign DOUT = CS5 ? reg16_ld_6_p3 : 16'bz;  // Controlled_Buffer controlled_buffer_6
  // REG16_LD reg16_ld_7: pin names not known; wires that end beside it: CLK, DIN, reg16_ld_7_p3, reg16_ld_7_p4
  assign DOUT = CS6 ? reg16_ld_7_p3 : 16'bz;  // Controlled_Buffer controlled_buffer_7
  // REG16_LD reg16_ld_8: pin names not known; wires that end beside it: CLK, DIN, reg16_ld_8_p3, reg16_ld_8_p4
  assign DOUT = CS7 ? reg16_ld_8_p3 : 16'bz;  // Controlled_Buffer controlled_buffer_8
  and and_5 (reg16_ld_5_p4, CS4, WR);
  and and_6 (reg16_ld_6_p4, CS5, WR);
  and and_7 (reg16_ld_7_p4, CS6, WR);
  and and_8 (reg16_ld_8_p4, CS7, WR);
  // REG16_LD reg16_ld_9: pin names not known; wires that end beside it: CLK, DIN, reg16_ld_9_p3, reg16_ld_9_p4
  assign DOUT = CS8 ? reg16_ld_9_p3 : 16'bz;  // Controlled_Buffer controlled_buffer_9
  // REG16_LD reg16_ld_10: pin names not known; wires that end beside it: CLK, DIN, reg16_ld_10_p3, reg16_ld_10_p4
  assign DOUT = CS9 ? reg16_ld_10_p3 : 16'bz;  // Controlled_Buffer controlled_buffer_10
  // REG16_LD reg16_ld_11: pin names not known; wires that end beside it: CLK, DIN, reg16_ld_11_p3, reg16_ld_11_p4
  assign DOUT = CS10 ? reg16_ld_11_p3 : 16'bz;  // Controlled_Buffer controlled_buffer_11
  // REG16_LD reg16_ld_12: pin names not known; wires that end beside it: CLK, DIN, reg16_ld_12_p3, reg16_ld_12_p4
  assign DOUT = CS11 ? reg16_ld_12_p3 : 16'bz;  // Controlled_Buffer controlled_buffer_12
  and and_9 (reg16_ld_9_p4, CS8, WR);
  and and_10 (reg16_ld_10_p4, CS9, WR);
  and and_11 (reg16_ld_11_p4, CS10, WR);
  and and_12 (reg16_ld_12_p4, CS11, WR);
  // REG16_LD reg16_ld_13: pin names not known; wires that end beside it: CLK, DIN, reg16_ld_13_p3, reg16_ld_13_p4
  assign DOUT = CS12 ? reg16_ld_13_p3 : 16'bz;  // Controlled_Buffer controlled_buffer_13
  // REG16_LD reg16_ld_14: pin names not known; wires that end beside it: CLK, DIN, reg16_ld_14_p3, reg16_ld_14_p4
  assign DOUT = CS13 ? reg16_ld_14_p3 : 16'bz;  // Controlled_Buffer controlled_buffer_14
  // REG16_LD reg16_ld_15: pin names not known; wires that end beside it: CLK, DIN, reg16_ld_15_p3, reg16_ld_15_p4
  assign DOUT = CS14 ? reg16_ld_15_p3 : 16'bz;  // Controlled_Buffer controlled_buffer_15
  // REG16_LD reg16_ld_16: pin names not known; wires that end beside it: CLK, DIN, reg16_ld_16_p3, reg16_ld_16_p4
  assign DOUT = CS15 ? reg16_ld_16_p3 : 16'bz;  // Controlled_Buffer controlled_buffer_16
  and and_13 (reg16_ld_13_p4, CS12, WR);
  and and_14 (reg16_ld_14_p4, CS13, WR);
  and and_15 (reg16_ld_15_p4, CS14, WR);
  and and_16 (reg16_ld_16_p4, CS15, WR);

  // Notes on the sheet:
  //   ACC == R[0]
  //   SP == R[1]
  //   PC == R[2]
endmodule

module ROM22x28 (
  input  [4:0] in_1,
  input  in_2,
  output [27:0] out_3
);

  ROM #(.addrWidth(5), .dataWidth(28)) rom_1 (.addr(in_1), .data(out_3), .sel(in_2));
endmodule

module ROM24x32 (
  input  [4:0] in_1,
  input  in_2,
  output [31:0] out_3
);

  ROM #(.addrWidth(5), .dataWidth(32)) rom_1 (.addr(in_1), .data(out_3), .sel(in_2));
endmodule

module KMADDR (
  input  in_1,
  input  in_2,
  input  in_3,
  input  in_4,
  input  in_5,
  input  in_6,
  output [4:0] out_7
);

  assign out_7 = in_1 ? 5'b00010 : 5'bz;  // Controlled_Buffer immed
  assign out_7 = in_2 ? 5'b00100 : 5'bz;  // Controlled_Buffer memdir
  assign out_7 = in_3 ? 5'b00101 : 5'bz;  // Controlled_Buffer regdir
  assign out_7 = in_4 ? 5'b00111 : 5'bz;  // Controlled_Buffer memind
  assign out_7 = in_5 ? 5'b01101 : 5'bz;  // Controlled_Buffer postincr
  assign out_7 = in_6 ? 5'b10000 : 5'bz;  // Controlled_Buffer pcrelpom
endmodule

module ALU_16_SUB_NOT_AND (
  input  Cin,
  input  \and ,
  input  [15:0] A,
  input  [15:0] B,
  input  sub,
  input  \not ,
  output [15:0] F,
  output Cout
);

  wire subtractor_1_bout;
  wire [15:0] and_1_out, not_1_out, subtractor_1_out;

  Subtractor #(.width(16)) subtractor_1 (.a(A), .b(B), .out(subtractor_1_out), .bin(Cin), .bout(subtractor_1_bout));
  assign not_1_out = ~B;  // NOT_Gate not_1, 16 bits wide
  assign and_1_out = A & B;  // AND_Gate and_1, 16 bits wide
  assign F = sub ? subtractor_1_out : 16'bz;  // Controlled_Buffer controlled_buffer_1
  assign Cout = sub ? subtractor_1_bout : 1'bz;  // Controlled_Buffer controlled_buffer_2
  assign F = \not  ? not_1_out : 16'bz;  // Controlled_Buffer controlled_buffer_3
  assign F = \and  ? and_1_out : 16'bz;  // Controlled_Buffer controlled_buffer_4
endmodule

module KMOPR_2 (
  input  LD,
  input  ST,
  input  SUB,
  input  AND,
  input  NOT,
  input  JMP,
  input  JSR,
  input  JLEQ,
  input  BNEQ,
  input  BGRTU,
  input  BNCR,
  input  BLSS,
  input  in_13,
  input  RTS,
  input  RTI,
  input  ASL,
  input  in_17,
  input  in_18,
  input  in_19,
  input  in_20,
  output [7:0] Adr7__0
);

  assign Adr7__0 = LD ? 8'h31 : 8'bz;  // Controlled_Buffer controlled_buffer_1
  assign Adr7__0 = ST ? 8'h33 : 8'bz;  // Controlled_Buffer controlled_buffer_2
  assign Adr7__0 = RTI ? 8'ha : 8'bz;  // Controlled_Buffer controlled_buffer_3
  assign Adr7__0 = RTS ? 8'h3 : 8'bz;  // Controlled_Buffer controlled_buffer_4
  assign Adr7__0 = SUB ? 8'h3d : 8'bz;  // Controlled_Buffer controlled_buffer_5
  assign Adr7__0 = ASL ? 8'h4 : 8'bz;  // Controlled_Buffer controlled_buffer_6
  assign Adr7__0 = AND ? 8'h40 : 8'bz;  // Controlled_Buffer controlled_buffer_7
  assign Adr7__0 = in_17 ? 8'h13 : 8'bz;  // Controlled_Buffer controlled_buffer_8
  assign Adr7__0 = NOT ? 8'h43 : 8'bz;  // Controlled_Buffer controlled_buffer_9
  assign Adr7__0 = JMP ? 8'h24 : 8'bz;  // Controlled_Buffer controlled_buffer_10
  assign Adr7__0 = JSR ? 8'h2a : 8'bz;  // Controlled_Buffer controlled_buffer_11
  assign Adr7__0 = JLEQ ? 8'h25 : 8'bz;  // Controlled_Buffer controlled_buffer_12
  assign Adr7__0 = in_18 ? 8'h17 : 8'bz;  // Controlled_Buffer controlled_buffer_13
  assign Adr7__0 = BNEQ ? 8'h23 : 8'bz;  // Controlled_Buffer controlled_buffer_14
  assign Adr7__0 = BGRTU ? 8'h21 : 8'bz;  // Controlled_Buffer controlled_buffer_15
  assign Adr7__0 = in_19 ? 8'h45 : 8'bz;  // Controlled_Buffer controlled_buffer_16
  assign Adr7__0 = BNCR ? 8'h1f : 8'bz;  // Controlled_Buffer controlled_buffer_17
  assign Adr7__0 = BLSS ? 8'h1d : 8'bz;  // Controlled_Buffer controlled_buffer_18
  assign Adr7__0 = in_20 ? 8'h4f : 8'bz;  // Controlled_Buffer controlled_buffer_19
  assign Adr7__0 = in_13 ? 8'h1b : 8'bz;  // Controlled_Buffer controlled_buffer_20

  // Notes on the sheet:
  //   HALT
  //   LOOPGRE
  //   ROLC
  //   PUSHGPR
  //   POPGPR
endmodule

module ROM256x35 (
  input  [7:0] A7__0,
  input  CS,
  output [7:0] DOUT43__36,
  output [31:0] DOUT_31__0,
  output [3:0] DOUT35__32
);

  ROM rom_1 (.addr(A7__0), .data(DOUT43__36), .sel(CS));
  ROM #(.dataWidth(4)) rom_2 (.addr(A7__0), .data(DOUT35__32), .sel(CS));
  ROM #(.dataWidth(32)) rom_3 (.addr(A7__0), .data(DOUT_31__0), .sel(CS));
endmodule

module ROM8x32 (
  input  [7:0] in_1,
  input  in_2,
  output [31:0] out_3
);

  ROM #(.dataWidth(32)) rom_1 (.addr(in_1), .data(out_3), .sel(in_2));
endmodule
