// Logisim project ORT2Project.circ as structural Verilog: 8 circuits, main circuit COMPUTER
module COMPUTER (
);

  wire BTN_RST_out, CLK, cpu_1_inta, interrupt_interface_4_1_p4, interrupt_interface_4_1_p5,
       interrupt_interface_4_1_p6, interrupt_interface_4_1_p7, pull_resistor_4_node, pull_resistor_5_node,
       ram_1_out_8, rst;
  wire [1:0] cpu_1_uext1__0;
  wire [3:0] interrupt_interface_4_1_p1;
  wire [7:0] pull_resistor_3_node, ram_1_out_7;
  wire [15:0] pull_resistor_2_node;

  Button BTN_RST (.out(BTN_RST_out));
  Clock u_CLK (.out(CLK));
  // RisingEdge risingedge_1: pin names not known; wires that end beside it: BTN_RST_out, CLK, rst
  RAM ram_1 (
    .in_1(pull_resistor_2_node), .in_2(CLK), .in_3(pull_resistor_3_node), .in_4(pull_resistor_4_node),
    .in_5(pull_resistor_5_node), .in_6(rst), .out_7(ram_1_out_7), .out_8(ram_1_out_8));
  Pull_Resistor pull_resistor_1 (.node(ram_1_out_7));
  Pull_Resistor pull_resistor_2 (.node(pull_resistor_2_node));
  Pull_Resistor pull_resistor_3 (.node(pull_resistor_3_node));
  Pull_Resistor pull_resistor_4 (.node(pull_resistor_4_node));
  Pull_Resistor pull_resistor_5 (.node(pull_resistor_5_node));
  Pull_Resistor pull_resistor_6 (.node(ram_1_out_8));
  CPU cpu_1 (
    .in_1(rst), .in_2(CLK), .in_3(ram_1_out_8), .in_4(ram_1_out_7), .ABUS(pull_resistor_2_node),
    .DOUTBUS(pull_resistor_3_node), .out_8(pull_resistor_4_node), .out_9(pull_resistor_5_node),
    .inta(cpu_1_inta), .intr3__0(interrupt_interface_4_1_p1), .UEXT1__0(cpu_1_uext1__0));
  // INTERRUPT_INTERFACE_4 interrupt_interface_4_1: pin names not known; wires that end beside it: interrupt_interface_4_1_p1, cpu_1_inta, cpu_1_uext1__0, interrupt_interface_4_1_p4, interrupt_interface_4_1_p5, interrupt_interface_4_1_p6, interrupt_interface_4_1_p7, CLK
  Button BTN_INTR3 (.out(interrupt_interface_4_1_p4));
  Button BTN_INTR2 (.out(interrupt_interface_4_1_p5));
  Button BTN_INTR1 (.out(interrupt_interface_4_1_p6));
  Button BTN_INTR0 (.out(interrupt_interface_4_1_p7));
endmodule

module CPU (
  input  in_1,
  input  in_2,
  input  in_3,
  input  [7:0] in_4,
  input  [3:0] intr3__0,
  output [15:0] ABUS,
  output [7:0] DOUTBUS,
  output out_8,
  output out_9,
  output inta,
  output [1:0] UEXT1__0
);

  wire aluC, common_1_out_17, done0, done1, grinst;
  wire [3:0] common_1_phaseffbus;
  wire [5:0] common_1_addrbus, pull_resistor_1_node;
  wire [7:0] pull_resistor_6_node;
  wire [14:0] pull_resistor_4_node;
  wire [15:0] A, ALU, B, INTRADDR, PSW;
  wire [19:0] common_1_instrucbus;
  wire [31:0] pull_resistor_5_node;

  COMMON common_1 (
    .CLK(in_2), .RST(in_1), .DIN(in_4), .CMEMBUS(pull_resistor_4_node), .MAR(ABUS), .MDR(DOUTBUS),
    .PHASEFFBUS(common_1_phaseffbus), .INSTRUCBUS(common_1_instrucbus), .ADDRBUS(common_1_addrbus),
    .PSW(PSW), .CREGBUS(pull_resistor_5_node), .CFFBUS(pull_resistor_6_node), .B(B),
    .CPSW(pull_resistor_1_node), .IVTPPDSP(INTRADDR), .out_17(common_1_out_17), .ALU(ALU), .A(A),
    .out_18(done0), .out_19(done1), .ALUC(aluC));
  Pull_Resistor pull_resistor_1 (.node(pull_resistor_1_node));
  Pull_Resistor pull_resistor_2 (.node(common_1_phaseffbus));
  Pull_Resistor pull_resistor_3 (.node(common_1_instrucbus));
  Pull_Resistor pull_resistor_4 (.node(pull_resistor_4_node));
  Pull_Resistor pull_resistor_5 (.node(pull_resistor_5_node));
  Pull_Resistor pull_resistor_6 (.node(pull_resistor_6_node));
  Pull_Resistor pull_resistor_7 (.node(common_1_addrbus));
  FETCH fetch_1 (
    .in_1(in_1), .in_2(in_2), .in_3(in_3), .PHASEFFBUS(common_1_phaseffbus),
    .INSTRUCBUS(common_1_instrucbus), .ADDRBUS(common_1_addrbus), .PSW(PSW), .rdMEM(out_9),
    .CMEMBUS(pull_resistor_4_node), .CFFBUS(pull_resistor_6_node), .CREGBUS(pull_resistor_5_node),
    .in_8(common_1_out_17), .out_9(grinst));
  ADDR addr_1 (
    .in_1(in_1), .in_2(in_2), .in_3(in_3), .PHASEFFBUS(common_1_phaseffbus),
    .INSTRUCBUS(common_1_instrucbus), .rdMEM(out_9), .CMEMBUS(pull_resistor_4_node),
    .CFFBUS(pull_resistor_6_node), .CREGBUS(pull_resistor_5_node), .ADDRBUS(common_1_addrbus));
  EXEC exec_1 (
    .in_4(in_1), .in_5(in_2), .in_6(in_3), .B(B), .PHASEFFBUS(common_1_phaseffbus),
    .INSTRUCBUS(common_1_instrucbus), .PSW(PSW), .ALU(ALU), .CMEMBUS(pull_resistor_4_node),
    .CFFBUS(pull_resistor_6_node), .CREGBUS(pull_resistor_5_node), .CPSW(pull_resistor_1_node),
    .rdMEM(out_9), .wrMEM(out_8), .ADDRBUS(common_1_addrbus), .in_1(grinst), .A(A), .in_2(done0),
    .in_3(done1), .out_20(aluC));
  INTR intr_1 (
    .in_1(in_1), .in_2(in_2), .in_3(in_3), .PHASEFFBUS(common_1_phaseffbus), .PSW(PSW), .intr(intr3__0),
    .ADDIVTP(INTRADDR), .CMEMBUS(pull_resistor_4_node), .CFFBUS(pull_resistor_6_node),
    .CREGBUS(pull_resistor_5_node), .rdMEM(out_9), .wrMEM(out_8), .UEXT1__0(UEXT1__0), .inta(inta));  // open: INSTRUCBUS

  // Other names for the same wires on the sheet: CLK = in_2; DIN7__0[7:0] = in_4; FCBUS = in_3; MAR[15:0] = ABUS;
  //   MDR[7:0] = DOUTBUS; RD = out_9; rst = in_1; WR = out_8
endmodule

module COMMON (
  input  CLK,
  input  RST,
  input  [7:0] DIN,
  input  [15:0] ALU,
  input  [15:0] IVTPPDSP,
  input  [14:0] CMEMBUS,
  input  [7:0] CFFBUS,
  input  [31:0] CREGBUS,
  input  [5:0] CPSW,
  input  ALUC,
  output [15:0] MAR,
  output [7:0] MDR,
  output [3:0] PHASEFFBUS,
  output [15:0] PSW,
  output [15:0] B,
  output [15:0] A,
  output out_17,
  output out_18,
  output out_19,
  output [5:0] ADDRBUS,
  output [19:0] INSTRUCBUS
);

  wire A15, add16_1_p3, addr_t, Amin, and_1_out, and_2_out, and_3_out, and_6_out, and_7_out, and_8_out,
       and_13_out, and_14_out, and_15_out, and_16_out, and_17_out, and_18_out, and_19_out, and_20_out,
       and_21_out, and_22_out, and_23_out, and_25_out, and_26_out, and_27_out, and_28_out, and_29_out,
       and_30_out, and_31_out, and_32_out, and_33_out, and_34_out, and_35_out, and_36_out, and_37_out,
       and_38_out, and_39_out, and_40_out, and_41_out, and_42_out, Azero, bezadr, brnch, decC, grintr1a,
       grintr1b, grintr1c, grintr1d, grintr1e, grintr1f, grintr1g, grintr1h, grintr1i, grintr1j, grintr1k,
       grintr1l, grintr2a, grintr2b, jmp_t, mp4_16b_1_p6, mp8_8b_1_p8, mp8_16b_1_p9, not_1_out, not_3_out,
       not_4_out, not_5_out, not_6_out, not_7_out, or_1_out, or_2_out, or_3_out, or_4_out, or_6_out,
       or_7_out, or_8_out, or_9_out, or_10_out, or_11_out, or_12_out, or_13_out, or_14_out, or_15_out,
       or_16_out, or_17_out, or_18_out, or_19_out, or_20_out, reg4m_dec_ld_1_p4, reg4m_dec_ld_1_p5,
       reg4m_inc_ld_1_p4, reg4m_inc_ld_1_p6, reg4m_inc_ld_1_p7, reg16_1_p7, rsff_1_p4, rsff_3_p4, rsff_4_p4,
       rsff_5_p4;
  wire [3:0] IR19__16, mp8_4b_1_p8, PG0cntrl, PG15cntrl;
  wire [7:0] IR7__0, IR15__8, IR31__24;
  wire [7:4] IR23__16;
  wire [14:0] REG;
  wire [15:0] ADDR_ADD, DW, mp8_16b_2_p9;

  // REG8_LD reg8_ld_1: pin names not known; wires that end beside it: CLK, MDR, IR31__24, CREGBUS[7]
  not not_1 (not_1_out, RST);
  // REG8_LD reg8_ld_2: pin names not known; wires that end beside it: CLK, MDR, {IR23__16, IR19__16}, CREGBUS[6]
  and and_1 (and_1_out, addr_t, and_8_out);
  // DC3_8 addr: pin names not known; wires that end beside it: IR31__24[2:0], and_1_out, INSTRUCBUS[15], INSTRUCBUS[16], INSTRUCBUS[17], INSTRUCBUS[18], INSTRUCBUS[19], grintr1a, grintr1b, grintr1c
  // MP8_16b mp8_16b_1: pin names not known; wires that end beside it: CMEMBUS[9], CMEMBUS[3], CMEMBUS[4], A, {IR7__0, IR15__8}, {IR7__0, IR15__8}, DW, ADDR_ADD, mp8_16b_1_p9, IVTPPDSP, 1'b1
  // REG16_INC_LD reg16_inc_ld_1: pin names not known; wires that end beside it: CLK, not_1_out, mp8_16b_1_p9, MAR, CMEMBUS[0], CMEMBUS[1]
  and and_2 (and_2_out, jmp_t, and_8_out);
  // DC3_8 jmp: pin names not known; wires that end beside it: IR31__24[2:0], and_2_out, INSTRUCBUS[13], INSTRUCBUS[14], grintr1d, grintr1e, grintr1f, grintr1g, grintr1h, grintr1i
  // RSFF rsff_1: pin names not known; wires that end beside it: CREGBUS[7], CLK, CREGBUS[6], rsff_1_p4
  // NOT_Gate not_2 has open pins: in=RST, out=open
  not not_3 (not_3_out, RST);
  // REG8_LD reg8_ld_3: pin names not known; wires that end beside it: CLK, MDR, IR15__8, CREGBUS[5]
  // DC2_4 dc2_4_1: pin names not known; wires that end beside it: addr_t, jmp_t, IR31__24[5:4], brnch, bezadr, PSW[0]
  and and_3 (and_3_out, and_1_out, rsff_1_p4);
  // MP4_16b mp4_16b_1: pin names not known; wires that end beside it: CREGBUS[18], CREGBUS[19], {A15, REG}, {IR7__0, IR15__8}, {IR7__0, IR15__8}, mp4_16b_1_p6, DW, 1'b1
  // REG16_INC_LD reg16_inc_ld_2: pin names not known; wires that end beside it: CLK, not_3_out, mp4_16b_1_p6, B, CREGBUS[17]
  and and_4 (out_18, PG0cntrl[0], PG0cntrl[1], PG0cntrl[2], PG0cntrl[3]);
  and and_5 (out_19, ~PG15cntrl[0], ~PG15cntrl[1], ~PG15cntrl[2], ~PG15cntrl[3]);  // AND_Gate
  and and_6 (and_6_out, brnch, and_8_out);
  // DC3_8 brnch: pin names not known; wires that end beside it: IR31__24[2:0], and_6_out, INSTRUCBUS[7], INSTRUCBUS[8], INSTRUCBUS[9], INSTRUCBUS[10], INSTRUCBUS[11], INSTRUCBUS[12], grintr1j, grintr1k
  and and_7 (and_7_out, bezadr, and_8_out);
  // DC3_8 bezadr: pin names not known; wires that end beside it: IR31__24[2:0], and_7_out, INSTRUCBUS[0], INSTRUCBUS[1], INSTRUCBUS[2], INSTRUCBUS[3], INSTRUCBUS[4], INSTRUCBUS[5], INSTRUCBUS[6], grintr1l
  // DC3_8 AM: pin names not known; wires that end beside it: IR23__16[7:5], and_3_out, grintr2a, ADDRBUS[0], ADDRBUS[1], ADDRBUS[2], ADDRBUS[3], grintr2b, ADDRBUS[4], ADDRBUS[5]
  // MP8_8b mp8_8b_1: pin names not known; wires that end beside it: CMEMBUS[5], CMEMBUS[6], CMEMBUS[7], DIN, {A15, REG[14:8]}, REG[7:0], PSW[15:8], mp8_8b_1_p8, PSW[7:0], 1'b1
  // REG8_LD reg8_ld_4: pin names not known; wires that end beside it: CLK, mp8_8b_1_p8, MDR, CMEMBUS[2]
  // REG8_LD reg8_ld_5: pin names not known; wires that end beside it: CLK, MDR, IR7__0, CREGBUS[4]
  and and_8 (and_8_out, ~IR31__24[7], ~IR31__24[6], ~IR31__24[3]);  // AND_Gate
  // REG4m_INC_LD reg4m_inc_ld_1: pin names not known; wires that end beside it: CLK, 4'b0000, PG0cntrl, reg4m_inc_ld_1_p4, reg4m_inc_ld_1_p4, reg4m_inc_ld_1_p6, reg4m_inc_ld_1_p7
  not not_4 (not_4_out, and_8_out);
  and and_9 (reg4m_inc_ld_1_p6, CREGBUS[15], INSTRUCBUS[5]);
  and and_10 (reg4m_inc_ld_1_p7, CREGBUS[14], INSTRUCBUS[5]);
  // MP8_4b mp8_4b_1: pin names not known; wires that end beside it: CREGBUS[9], CREGBUS[10], CREGBUS[11], 4'b0010, 4'b0001, 4'b0000, IR19__16, mp8_4b_1_p8, PG0cntrl, PG15cntrl, 1'b1
  or or_1 (or_1_out, grintr1a, grintr1b, grintr1c, grintr1d, grintr1e, grintr1f);
  not not_5 (not_5_out, RST);
  // REG8_INC_LD reg8_inc_ld_1: pin names not known; wires that end beside it: CLK, not_5_out, MDR, DW[15:8], CREGBUS[0]
  // REG4m_DEC_LD reg4m_dec_ld_1: pin names not known; wires that end beside it: CLK, 4'b1111, PG15cntrl, reg4m_dec_ld_1_p4, reg4m_dec_ld_1_p5
  not not_6 (not_6_out, RST);
  // RSFF rsff_2: pin names not known; wires that end beside it: CFFBUS[1], CLK, CFFBUS[0], not_6_out, PHASEFFBUS[0]
  and and_11 (reg4m_dec_ld_1_p4, CREGBUS[15], INSTRUCBUS[6]);
  and and_12 (reg4m_dec_ld_1_p5, CREGBUS[14], INSTRUCBUS[5]);
  or or_2 (or_2_out, grintr1g, grintr1h, grintr1i, grintr1j, grintr1k, grintr1l);
  GPR16x16_ACC_SP_PC gpr16x16_acc_sp_pc_1 (
    .CLK(CLK), .WR(CREGBUS[8]), .DIN(mp8_16b_2_p9), .ADDR(mp8_4b_1_p8), .rst(RST), .DOUT({A15, REG}));
  // REG16 reg16_1: pin names not known; wires that end beside it: decC, CLK, {A15, REG}, A, CREGBUS[2], CREGBUS[13], reg16_1_p7, CREGBUS[3], CREGBUS[12]
  or or_3 (or_3_out, or_2_out, or_1_out);
  or or_4 (or_4_out, grintr2a, grintr2b);
  // ADD16 add16_1: pin names not known; wires that end beside it: {A15, REG}, ADDR_ADD, add16_1_p3
  not not_7 (not_7_out, RST);
  // REG8_INC_LD reg8_inc_ld_2: pin names not known; wires that end beside it: CLK, not_7_out, MDR, DW[7:0], CREGBUS[1]
  // MP8_16b mp8_16b_2: pin names not known; wires that end beside it: CREGBUS[20], CREGBUS[21], CREGBUS[22], A, B, DW, {IR15__8, IR23__16, IR19__16}, {IR15__8, IR23__16, IR19__16}, mp8_16b_2_p9, ADDR_ADD, ALU, 1'b1
  or or_5 (out_17, not_4_out, or_3_out, or_4_out);
  // MP2_16b mp2_16b_1: pin names not known; wires that end beside it: CMEMBUS[8], {{9{IR15__8[7]}}, IR15__8[6:0]}, add16_1_p3, {{9{IR23__16[7]}}, IR23__16[6:4], IR19__16}, 1'b1
  // RSFF rsff_3: pin names not known; wires that end beside it: CFFBUS[3], CLK, CFFBUS[2], rsff_3_p4, PHASEFFBUS[1]
  not not_8 (rsff_3_p4, RST);
  // MP2_1b mp2_1b_1: pin names not known; wires that end beside it: INSTRUCBUS[3], PSW[4], reg16_1_p7, 1'b0, 1'b1, {A15, REG}
  or or_6 (or_6_out, INSTRUCBUS[3], INSTRUCBUS[4]);
  or or_7 (or_7_out, INSTRUCBUS[3], INSTRUCBUS[4], INSTRUCBUS[12], INSTRUCBUS[15], INSTRUCBUS[17], INSTRUCBUS[18], INSTRUCBUS[19]);
  or or_8 (or_8_out, INSTRUCBUS[3], INSTRUCBUS[4], INSTRUCBUS[12], INSTRUCBUS[15], INSTRUCBUS[17], INSTRUCBUS[18], INSTRUCBUS[19]);
  and and_13 (and_13_out, ~A15, B[15], ALU[15]);  // AND_Gate
  or or_9 (or_9_out, and_13_out, and_14_out);
  and and_14 (and_14_out, A15, ~B[15], ~ALU[15]);  // AND_Gate
  and and_15 (and_15_out, decC, INSTRUCBUS[12]);
  and and_16 (and_16_out, ALUC, INSTRUCBUS[17]);
  and and_17 (and_17_out, A15, or_6_out);
  // RSFF rsff_4: pin names not known; wires that end beside it: CFFBUS[5], CLK, CFFBUS[4], rsff_4_p4, PHASEFFBUS[2]
  not not_9 (rsff_4_p4, RST);
  and and_18 (and_18_out, Azero, or_7_out);
  and and_19 (and_19_out, A15, or_8_out);
  and and_20 (and_20_out, INSTRUCBUS[12], Amin);
  or or_10 (or_10_out, and_20_out, and_21_out);
  and and_21 (and_21_out, or_9_out, INSTRUCBUS[17]);
  or or_11 (or_11_out, and_15_out, and_16_out, and_17_out);
  and and_22 (and_22_out, CREGBUS[24], ~MDR[0]);  // AND_Gate
  and and_23 (and_23_out, CREGBUS[24], MDR[0]);
  and and_24 (Azero, ~REG[0], ~REG[1], ~REG[2], ~REG[3], ~REG[4], ~REG[5], ~REG[6], ~REG[7], ~REG[8], ~REG[9], ~REG[10], ~REG[11], ~REG[12], ~REG[13], ~REG[14], ~A15);  // AND_Gate
  and and_25 (and_25_out, CREGBUS[24], ~MDR[1]);  // AND_Gate
  and and_26 (and_26_out, CREGBUS[24], MDR[1]);
  and and_27 (and_27_out, CPSW[2], ~and_18_out);  // AND_Gate
  and and_28 (and_28_out, CPSW[2], and_18_out);
  and and_29 (and_29_out, CREGBUS[24], ~MDR[2]);  // AND_Gate
  and and_30 (and_30_out, CREGBUS[24], MDR[2]);
  and and_31 (and_31_out, CPSW[1], ~and_19_out);  // AND_Gate
  and and_32 (and_32_out, CPSW[1], and_19_out);
  and and_33 (and_33_out, CREGBUS[24], ~MDR[3]);  // AND_Gate
  and and_34 (and_34_out, CREGBUS[24], MDR[3]);
  and and_35 (and_35_out, CPSW[4], ~or_10_out);  // AND_Gate
  and and_36 (and_36_out, CPSW[4], or_10_out);
  and and_37 (and_37_out, CREGBUS[23], ~MDR[7]);  // AND_Gate
  and and_38 (and_38_out, CREGBUS[23], MDR[7]);
  and and_39 (and_39_out, CREGBUS[24], ~MDR[4]);  // AND_Gate
  and and_40 (and_40_out, CREGBUS[24], MDR[4]);
  and and_41 (and_41_out, CPSW[3], ~or_11_out);  // AND_Gate
  and and_42 (and_42_out, CPSW[3], or_11_out);
  or or_12 (or_12_out, CPSW[0], and_22_out);
  // RSFF rsff_5: pin names not known; wires that end beside it: CFFBUS[7], CLK, CFFBUS[6], rsff_5_p4, PHASEFFBUS[3]
  not not_10 (rsff_5_p4, RST);
  or or_13 (or_13_out, and_25_out, and_27_out);
  or or_14 (or_14_out, and_28_out, and_26_out);
  or or_15 (or_15_out, and_29_out, and_31_out);
  or or_16 (or_16_out, and_32_out, and_30_out);
  or or_17 (or_17_out, and_33_out, and_35_out);
  or or_18 (or_18_out, and_36_out, and_34_out);
  or or_19 (or_19_out, and_39_out, and_41_out);
  or or_20 (or_20_out, and_42_out, and_40_out);
  // NOT_Gate not_11 has open pins: in=RST, out=open
  // RSFF rsff_6: pin names not known; wires that end beside it: and_37_out, CLK, and_38_out, PSW[15]
  // NOT_Gate not_12 has open pins: in=RST, out=open
  // RSFF rsff_7: pin names not known; wires that end beside it: or_12_out, CLK, and_23_out, PSW[0]
  and and_43 (Amin, ~REG[0], ~REG[1], ~REG[2], ~REG[3], ~REG[4], ~REG[5], ~REG[6], ~REG[7], ~REG[8], ~REG[9], ~REG[10], ~REG[11], ~REG[12], ~REG[13], ~REG[14], A15);  // AND_Gate
  // RSFF rsff_8: pin names not known; wires that end beside it: or_13_out, CLK, or_14_out, PSW[1]
  // NOT_Gate not_13 has open pins: in=RST, out=open
  // RSFF rsff_9: pin names not known; wires that end beside it: or_15_out, CLK, or_16_out, PSW[2]
  // NOT_Gate not_14 has open pins: in=RST, out=open
  // RSFF rsff_10: pin names not known; wires that end beside it: or_17_out, CLK, or_18_out, PSW[3]
  // NOT_Gate not_15 has open pins: in=RST, out=open
  // RSFF rsff_11: pin names not known; wires that end beside it: or_19_out, CLK, or_20_out, PSW[4]
  // NOT_Gate not_16 has open pins: in=RST, out=open

  // Other names for the same wires on the sheet: IR23__16[3:0] = IR19__16; immed = ADDRBUS[0]; memdir = ADDRBUS[1];
  //   regdir = ADDRBUS[2]; memind = ADDRBUS[3]; postincr = ADDRBUS[4]; pcrelpom = ADDRBUS[5]; ALU15__0[15:0] = ALU;
  //   stFETCH = CFFBUS[0]; clFETCH = CFFBUS[1]; stADDR = CFFBUS[2]; clADDR = CFFBUS[3]; stEXEC = CFFBUS[4];
  //   clEXEC = CFFBUS[5]; stINTR = CFFBUS[6]; clINTR = CFFBUS[7]; ldMAR = CMEMBUS[0]; incMAR = CMEMBUS[1];
  //   ldMDR = CMEMBUS[2]; mpMAR1 = CMEMBUS[3]; mpMAR0 = CMEMBUS[4]; mpMDR2 = CMEMBUS[5]; mpMDR1 = CMEMBUS[6];
  //   mpMDR0 = CMEMBUS[7]; mpADD = CMEMBUS[8]; mpMAR2 = CMEMBUS[9]; clPSWSTART = CPSW[0]; ldN = CPSW[1];
  //   ldZ = CPSW[2]; ldC = CPSW[3]; ldV = CPSW[4]; ldDWH = CREGBUS[0]; ldDWL = CREGBUS[1]; ldREG = CREGBUS[2];
  //   incREG = CREGBUS[3]; ldIR7__0 = CREGBUS[4]; ldIR15__8 = CREGBUS[5]; ldIR23__16 = CREGBUS[6];
  //   ldIR31__24 = CREGBUS[7]; wr = CREGBUS[8]; mpREG2 = CREGBUS[9]; mpREG1 = CREGBUS[10]; mpREG0 = CREGBUS[11];
  //   decREG = CREGBUS[12]; slREG = CREGBUS[13]; PGcntrl = CREGBUS[14]; ldPG = CREGBUS[15]; ldB = CREGBUS[17];
  //   mpB1 = CREGBUS[18]; mpB0 = CREGBUS[19]; mpREGIN2 = CREGBUS[20]; mpREGIN1 = CREGBUS[21]; mpREGIN0 = CREGBUS[22];
  //   ldPSWH = CREGBUS[23]; ldPSWL = CREGBUS[24]; Din7__0[7:0] = DIN; done0 = out_18; done15 = out_19;
  //   ENTRADDR15__0[15:0] = IVTPPDSP; grinstr = out_17; HALT = INSTRUCBUS[0]; RTS = INSTRUCBUS[1];
  //   RTI = INSTRUCBUS[2]; ASL = INSTRUCBUS[3]; ROLC = INSTRUCBUS[4]; PUSHGPR = INSTRUCBUS[5]; POPGPR = INSTRUCBUS[6];
  //   BLSS = INSTRUCBUS[7]; BNCR = INSTRUCBUS[8]; BGRTU = INSTRUCBUS[9]; BNEG = INSTRUCBUS[10]; JLEQ = INSTRUCBUS[11];
  //   LOOPGRE = INSTRUCBUS[12]; JMP = INSTRUCBUS[13]; JSR = INSTRUCBUS[14]; LD = INSTRUCBUS[15]; ST = INSTRUCBUS[16];
  //   SUB = INSTRUCBUS[17]; AND = INSTRUCBUS[18]; NOT = INSTRUCBUS[19]; MAR15__0[15:0] = MAR; MDR7__0[7:0] = MDR;
  //   OUTB[15:0] = B; FETCH = PHASEFFBUS[0]; ADDR = PHASEFFBUS[1]; EXEC = PHASEFFBUS[2]; INTR = PHASEFFBUS[3];
  //   PSW15__0[15:0] = PSW; PSWSTART = PSW[0]; PSWZ = PSW[1]; PSWN = PSW[2]; PSWV = PSW[3]; PSWC = PSW[4];
  //   PSWI = PSW[15]; REG[15] = A15; REGOUT[15:0] = A

  // Notes on the sheet:
  //   Instrukcijski registar
  //   MAR
  //   REGFILE
  //   Dekoderi za prepoznavanje instrukcije na osnovu sadrzaja registra IR23..16
  //   MDR
  //   PC SP ACC
  //   odavde se vade bitovi za NZCV
  //   Eout za PSWC pri dec
  //   FF za pokretanje FETCH, ADDR, EXEC i INTR faze izvršavanja instrukcije
  //   Programska statusna reč (PSW)
endmodule

module FETCH (
  input  in_1,
  input  in_2,
  input  in_3,
  input  [3:0] PHASEFFBUS,
  input  [19:0] INSTRUCBUS,
  input  [5:0] ADDRBUS,
  input  [15:0] PSW,
  input  in_8,
  output out_9,
  output [14:0] CMEMBUS,
  output [7:0] CFFBUS,
  output [31:0] CREGBUS,
  output rdMEM
);

  wire addr2, addr2cntrl, addr3, addr3cntrl, addr4, addr_t, and_1_out, and_2_out, and_5_out, and_6_out,
       and_7_out, and_8_out, and_9_out, and_10_out, and_11_out, and_12_out, and_13_out, and_14_out, bezadr1,
       bezadr1cntrl, brnch2, brnch2cntrl, brnchcnd, brnchuncnd, clFETCH, grinstcntrl, incREG, jmp3,
       jmp3cntrl, ldIR7__0, ldIR15__8, ldIR23__16, ldIR31__24, ldMAR, ldMDR, ldREG, not_1_out, notFCBUS,
       notSTARTandFETCH, or_5_out, or_6_out, or_8_out, or_9_out, rdMEM_t, reg8_inc_ld_1_p4, stADDR, stEXEC,
       wr;
  wire [3:0] rom22x28_1_out_3;
  wire [4:0] undriven;
  wire [7:0] reg8_inc_ld_1_p3;
  wire [15:13] rom22x28_1_out_3_2;

  not not_1 (not_1_out, in_1);
  or or_1 (brnch2, INSTRUCBUS[7], INSTRUCBUS[8], INSTRUCBUS[9], INSTRUCBUS[10]);
  or or_2 (jmp3, INSTRUCBUS[11], INSTRUCBUS[12], INSTRUCBUS[13], INSTRUCBUS[14]);
  // REG8_INC_LD reg8_inc_ld_1: pin names not known; wires that end beside it: in_2, not_1_out, reg8_inc_ld_1_p3, reg8_inc_ld_1_p4
  or or_3 (bezadr1, INSTRUCBUS[0], INSTRUCBUS[1], INSTRUCBUS[2], INSTRUCBUS[3], INSTRUCBUS[4], INSTRUCBUS[5], INSTRUCBUS[6]);
  // NOT_Gate not_2 has open pins: in=reg8_inc_ld_1_p4, out=open
  ROM22x28 rom22x28_1 (
    .in_1(undriven), .in_2(1'b1),
    .out_3({reg8_inc_ld_1_p3, rom22x28_1_out_3, rom22x28_1_out_3_2, stEXEC, stADDR, clFETCH, wr, ldIR7__0, ldIR15__8, ldIR23__16, ldIR31__24, ldMDR, rdMEM_t, incREG, ldMAR, ldREG}));
  or or_4 (reg8_inc_ld_1_p4, brnchuncnd, brnchcnd);
  // DC4_16 dc4_16_1: pin names not known; wires that end beside it: rom22x28_1_out_3, 1'b1, brnchuncnd, notSTARTandFETCH, notFCBUS, grinstcntrl, bezadr1cntrl, brnch2cntrl, addr2cntrl, jmp3cntrl, addr3cntrl
  or or_5 (or_5_out, INSTRUCBUS[15], INSTRUCBUS[17], INSTRUCBUS[18], INSTRUCBUS[19]);
  or or_6 (or_6_out, ADDRBUS[1], ADDRBUS[3]);
  or or_7 (addr_t, INSTRUCBUS[16], or_5_out);
  and and_1 (and_1_out, or_5_out, or_8_out);
  or or_8 (or_8_out, ADDRBUS[0], or_6_out);
  or or_9 (or_9_out, ADDRBUS[2], ADDRBUS[4]);
  and and_2 (and_2_out, PSW[0], PHASEFFBUS[0]);
  and and_3 (addr2, addr_t, or_9_out);
  and and_4 (addr3, addr_t, ADDRBUS[5]);
  and and_5 (and_5_out, ~and_2_out, notSTARTandFETCH);  // AND_Gate
  and and_6 (and_6_out, ~in_3, notFCBUS);  // AND_Gate
  and and_7 (and_7_out, grinstcntrl, out_9);
  and and_8 (and_8_out, bezadr1cntrl, bezadr1);
  and and_9 (and_9_out, brnch2cntrl, brnch2);
  and and_10 (and_10_out, addr2cntrl, addr2);
  and and_11 (and_11_out, jmp3cntrl, jmp3);
  and and_12 (and_12_out, addr3cntrl, addr3);
  and and_13 (and_13_out, INSTRUCBUS[16], or_6_out);
  or or_10 (addr4, and_13_out, and_1_out);
  or or_11 (brnchcnd, and_5_out, and_6_out, and_7_out, and_8_out, and_9_out, and_10_out, and_11_out, and_12_out);
  and and_14 (and_14_out, INSTRUCBUS[16], ADDRBUS[0]);
  or or_12 (out_9, in_8, and_14_out);
  assign CMEMBUS[0] = ldMAR ? 1'b1 : 1'bz;  // Controlled_Buffer controlled_buffer_1
  assign CMEMBUS[2] = ldMDR ? 1'b1 : 1'bz;  // Controlled_Buffer controlled_buffer_2
  assign CREGBUS[2] = ldREG ? 1'b1 : 1'bz;  // Controlled_Buffer controlled_buffer_3
  assign CREGBUS[3] = incREG ? 1'b1 : 1'bz;  // Controlled_Buffer controlled_buffer_4
  assign CREGBUS[4] = ldIR7__0 ? 1'b1 : 1'bz;  // Controlled_Buffer controlled_buffer_5
  assign CREGBUS[5] = ldIR15__8 ? 1'b1 : 1'bz;  // Controlled_Buffer controlled_buffer_6
  assign CREGBUS[6] = ldIR23__16 ? 1'b1 : 1'bz;  // Controlled_Buffer controlled_buffer_7
  assign CREGBUS[7] = ldIR31__24 ? 1'b1 : 1'bz;  // Controlled_Buffer controlled_buffer_8
  assign CREGBUS[8] = wr ? 1'b1 : 1'bz;  // Controlled_Buffer controlled_buffer_9
  assign CFFBUS[1] = clFETCH ? 1'b1 : 1'bz;  // Controlled_Buffer controlled_buffer_10
  assign CFFBUS[2] = stADDR ? 1'b1 : 1'bz;  // Controlled_Buffer controlled_buffer_11
  assign CFFBUS[4] = stEXEC ? 1'b1 : 1'bz;  // Controlled_Buffer controlled_buffer_12
  assign rdMEM = rdMEM_t ? 1'b1 : 1'bz;  // Controlled_Buffer controlled_buffer_13

  // Other names for the same wires on the sheet: immed = ADDRBUS[0]; memdir = ADDRBUS[1]; regdir = ADDRBUS[2];
  //   memind = ADDRBUS[3]; postincr = ADDRBUS[4]; pcrelpom = ADDRBUS[5]; CLK = in_2; FCBUS = in_3; grinst = out_9;
  //   grinstr = in_8; HALT = INSTRUCBUS[0]; RTS = INSTRUCBUS[1]; RTI = INSTRUCBUS[2]; ASL = INSTRUCBUS[3];
  //   ROLC = INSTRUCBUS[4]; PUSHGPR = INSTRUCBUS[5]; POPGPR = INSTRUCBUS[6]; BLSS = INSTRUCBUS[7];
  //   BNCR = INSTRUCBUS[8]; BGRTU = INSTRUCBUS[9]; BNEG = INSTRUCBUS[10]; JLEQ = INSTRUCBUS[11];
  //   LOOPGRE = INSTRUCBUS[12]; JMP = INSTRUCBUS[13]; JSR = INSTRUCBUS[14]; LD = INSTRUCBUS[15]; ST = INSTRUCBUS[16];
  //   SUB = INSTRUCBUS[17]; AND = INSTRUCBUS[18]; NOT = INSTRUCBUS[19]; FETCH = PHASEFFBUS[0]; ADDR = PHASEFFBUS[1];
  //   EXEC = PHASEFFBUS[2]; INTR = PHASEFFBUS[3]; PSWST = PSW[0]; rst = in_1

  // Notes on the sheet:
  //   Operaciona jedinica
  //   Kontrolna jedinica
endmodule

module ADDR (
  input  in_1,
  input  in_2,
  input  in_3,
  input  [3:0] PHASEFFBUS,
  input  [19:0] INSTRUCBUS,
  input  [5:0] ADDRBUS,
  output [14:0] CMEMBUS,
  output [7:0] CFFBUS,
  output [31:0] CREGBUS,
  output rdMEM
);

  wire and_1_out, and_2_out, and_3_out, brcase, brcnd, bruncond, clADDR, incMAR, incREG, ldB, ldDWH, ldDWL,
       ldMAR, ldMDR, ldREG, mp2_8b_1_p3, mpB0, mpB1, mpMAR0, mpMAR1, mpREG0, mpREG1, not_1_out, notADDR,
       notFCBUS, rdMEM_t, reg8_inc_ld_1_p5, reg8_inc_ld_1_p6, STcntrl, stEXEC, wr;
  wire [2:0] reg8_inc_ld_1_p4_2, rom24x32_1_out_3;
  wire [4:0] mp2_8b_1_p4, reg8_inc_ld_1_p4;
  wire [31:18] rom24x32_1_out_3_2;

  not not_1 (not_1_out, in_1);
  // MP2_8b mp2_8b_1: pin names not known; wires that end beside it: brcase, rom24x32_1_out_3_2[31:24], mp2_8b_1_p3, {3'b000, mp2_8b_1_p4}, 1'b1
  // REG8_INC_LD reg8_inc_ld_1: pin names not known; wires that end beside it: in_2, not_1_out, mp2_8b_1_p3, {reg8_inc_ld_1_p4_2, reg8_inc_ld_1_p4}, reg8_inc_ld_1_p5, reg8_inc_ld_1_p6
  KMADDR kmaddr_1 (
    .in_1(ADDRBUS[0]), .in_2(ADDRBUS[1]), .in_3(ADDRBUS[2]), .in_4(ADDRBUS[3]), .in_5(ADDRBUS[4]),
    .in_6(ADDRBUS[5]), .out_7(mp2_8b_1_p4));
  or or_1 (reg8_inc_ld_1_p5, brcase, bruncond, brcnd);
  not not_2 (reg8_inc_ld_1_p6, reg8_inc_ld_1_p5);
  ROM24x32 rom24x32_1 (
    .in_1(reg8_inc_ld_1_p4), .in_2(1'b1),
    .out_3({rom24x32_1_out_3_2[31:23], rom24x32_1_out_3, rom24x32_1_out_3_2[19:18], stEXEC, clADDR, wr, rdMEM_t, ldMDR, ldDWH, ldDWL, incREG, mpREG1, mpREG0, ldREG, incMAR, mpMAR1, mpMAR0, ldMAR, mpB1, mpB0, ldB}));
  // DC3_8 dc3_8_1: pin names not known; wires that end beside it: rom24x32_1_out_3, 1'b1, bruncond, notADDR, STcntrl, notFCBUS, brcase
  and and_1 (and_1_out, ~PHASEFFBUS[1], notADDR);  // AND_Gate
  and and_2 (and_2_out, STcntrl, INSTRUCBUS[16]);
  and and_3 (and_3_out, ~in_3, notFCBUS);  // AND_Gate
  or or_2 (brcnd, and_1_out, and_2_out, and_3_out);
  assign CMEMBUS[0] = ldMAR ? 1'b1 : 1'bz;  // Controlled_Buffer controlled_buffer_1
  assign CMEMBUS[1] = incMAR ? 1'b1 : 1'bz;  // Controlled_Buffer controlled_buffer_2
  assign CMEMBUS[2] = ldMDR ? 1'b1 : 1'bz;  // Controlled_Buffer controlled_buffer_3
  assign CMEMBUS[3] = mpMAR1 ? 1'b1 : 1'bz;  // Controlled_Buffer controlled_buffer_4
  assign CMEMBUS[4] = mpMAR0 ? 1'b1 : 1'bz;  // Controlled_Buffer controlled_buffer_5
  assign CFFBUS[3] = clADDR ? 1'b1 : 1'bz;  // Controlled_Buffer controlled_buffer_6
  assign CFFBUS[4] = stEXEC ? 1'b1 : 1'bz;  // Controlled_Buffer controlled_buffer_7
  assign CREGBUS[0] = ldDWH ? 1'b1 : 1'bz;  // Controlled_Buffer controlled_buffer_8
  assign CREGBUS[1] = ldDWL ? 1'b1 : 1'bz;  // Controlled_Buffer controlled_buffer_9
  assign CREGBUS[2] = ldREG ? 1'b1 : 1'bz;  // Controlled_Buffer controlled_buffer_10
  assign CREGBUS[3] = incREG ? 1'b1 : 1'bz;  // Controlled_Buffer controlled_buffer_11
  assign CREGBUS[8] = wr ? 1'b1 : 1'bz;  // Controlled_Buffer controlled_buffer_12
  assign CREGBUS[10] = mpREG1 ? 1'b1 : 1'bz;  // Controlled_Buffer controlled_buffer_13
  assign CREGBUS[11] = mpREG0 ? 1'b1 : 1'bz;  // Controlled_Buffer controlled_buffer_14
  assign CREGBUS[17] = ldB ? 1'b1 : 1'bz;  // Controlled_Buffer controlled_buffer_15
  assign CREGBUS[18] = mpB1 ? 1'b1 : 1'bz;  // Controlled_Buffer controlled_buffer_16
  assign CREGBUS[19] = mpB0 ? 1'b1 : 1'bz;  // Controlled_Buffer controlled_buffer_17
  assign rdMEM = rdMEM_t ? 1'b1 : 1'bz;  // Controlled_Buffer controlled_buffer_18

  // Other names for the same wires on the sheet: immed = ADDRBUS[0]; memdir = ADDRBUS[1]; regdir = ADDRBUS[2];
  //   memind = ADDRBUS[3]; postincr = ADDRBUS[4]; pcrelpom = ADDRBUS[5]; CLK = in_2; FCBUS = in_3;
  //   ST = INSTRUCBUS[16]; ADDR = PHASEFFBUS[1]; rst = in_1

  // Notes on the sheet:
  //   Upravljacka jedinica
  //   Operaciona jedinica
endmodule

module EXEC (
  input  in_1,
  input  in_2,
  input  in_3,
  input  in_4,
  input  in_5,
  input  in_6,
  input  [15:0] B,
  input  [15:0] A,
  input  [3:0] PHASEFFBUS,
  input  [19:0] INSTRUCBUS,
  input  [5:0] ADDRBUS,
  input  [15:0] PSW,
  output [15:0] ALU,
  output [14:0] CMEMBUS,
  output [7:0] CFFBUS,
  output [31:0] CREGBUS,
  output [5:0] CPSW,
  output rdMEM,
  output wrMEM,
  output out_20
);

  wire and_1_out, and_2_out, and_3_out, and_4_out, and_5_out, and_6_out, and_7_out, and_8_out, and_9_out,
       and_10_out, and_11_out, and_12_out, and_13_out, and_14_out, brbrorjmp, brcnd, brdone0, brdone15,
       brgrinst, brnotEXEC, bropr, brorjmp, brregdir, brRTI, bruncnond, clEXEC, clPSWST, decREG, incMAR,
       incREG, ldC, ldDWH, ldDWL, ldMAR, ldMDR, ldN, ldPG, ldPSWH, ldPSWL, ldREG, ldV, ldZ, mp2_8b_1_p3,
       mpADD, mpMDR0, mpMDR1, mpREG0, mpREG1, mpREG2, mpREGIN0, mpREGIN1, mpREGIN2, not_1_out, notFCBUS,
       or_2_out, or_3_out, PGcntrl, rdMEM_t, reg8_inc_ld_1_p5, slREG, stINTR, wr, wrMEM_t, xor_1_out,
       xor_2_out, xor_3_out;
  wire [3:0] rom256x35_1_dout35__32;
  wire [7:0] mp2_8b_1_p2, mp2_8b_1_p4, reg8_inc_ld_1_p4;

  ALU_16_SUB_NOT_AND alu_16_sub_not_and_1 (
    .Cin(1'b0), .A(A), .B(B), .sub(INSTRUCBUS[17]), .\not (INSTRUCBUS[19]), .\and (INSTRUCBUS[18]), .F(ALU),
    .Cout(out_20));
  not not_1 (not_1_out, in_4);
  // MP2_8b mp2_8b_1: pin names not known; wires that end beside it: bropr, mp2_8b_1_p2, mp2_8b_1_p3, mp2_8b_1_p4, 1'b1
  // REG8_INC_LD reg8_inc_ld_1: pin names not known; wires that end beside it: in_5, not_1_out, mp2_8b_1_p3, reg8_inc_ld_1_p4, reg8_inc_ld_1_p5
  // NOT_Gate not_2 has open pins: in=reg8_inc_ld_1_p5, out=open
  KMOPR kmopr_1 (
    .LD(INSTRUCBUS[15]), .ST(INSTRUCBUS[16]), .SUB(INSTRUCBUS[17]), .AND(INSTRUCBUS[18]),
    .NOT(INSTRUCBUS[19]), .JMP(INSTRUCBUS[13]), .JSR(INSTRUCBUS[14]), .JLEQ(INSTRUCBUS[12]),
    .BNEQ(INSTRUCBUS[11]), .BGRTU(INSTRUCBUS[10]), .BNCR(INSTRUCBUS[9]), .BLSS(INSTRUCBUS[8]),
    .in_13(INSTRUCBUS[7]), .RTS(INSTRUCBUS[0]), .RTI(INSTRUCBUS[1]), .ASL(INSTRUCBUS[2]),
    .in_17(INSTRUCBUS[3]), .Adr7__0(mp2_8b_1_p4), .in_18(INSTRUCBUS[4]), .in_19(INSTRUCBUS[5]),
    .in_20(INSTRUCBUS[6]));
  or or_1 (reg8_inc_ld_1_p5, brcnd, bruncnond, bropr);
  ROM256x35 rom256x35_1 (
    .A7__0(reg8_inc_ld_1_p4), .CS(1'b1), .DOUT35__32(rom256x35_1_dout35__32),
    .DOUT_31__0({wrMEM_t, ldV, ldC, ldZ, ldN, stINTR, clEXEC, clPSWST, incMAR, PGcntrl, ldPG, mpADD, mpMDR1, mpMDR0, mpREG2, mpREG1, mpREG0, mpREGIN2, mpREGIN1, mpREGIN0, wr, ldDWH, ldDWL, ldPSWH, ldPSWL, rdMEM_t, ldMDR, ldMAR, slREG, decREG, incREG, ldREG}),
    .DOUT43__36(mp2_8b_1_p2));
  xor xor_1 (xor_1_out, PSW[2], PSW[3]);
  // DC4_16 dc4_16_1: pin names not known; wires that end beside it: rom256x35_1_dout35__32, 1'b1, bruncnond, bropr, brgrinst, notFCBUS, brRTI, brbrorjmp, brregdir, brdone0, brdone15, brnotEXEC
  xor xor_2 (xor_2_out, PSW[2], PSW[3]);
  or or_2 (or_2_out, PSW[4], PSW[3]);
  or or_3 (or_3_out, xor_1_out, PSW[1]);
  xor xor_3 (xor_3_out, PSW[2], PSW[3]);
  and and_1 (and_1_out, xor_2_out, INSTRUCBUS[7]);
  and and_2 (and_2_out, ~PSW[4], INSTRUCBUS[8]);  // AND_Gate
  and and_3 (and_3_out, ~or_2_out, INSTRUCBUS[9]);  // AND_Gate
  and and_4 (and_4_out, PSW[2], INSTRUCBUS[10]);
  and and_5 (and_5_out, or_3_out, INSTRUCBUS[11]);
  and and_6 (and_6_out, ~xor_3_out, INSTRUCBUS[12]);  // AND_Gate
  or or_4 (brorjmp, and_1_out, and_2_out, and_3_out, and_4_out, and_5_out, and_6_out);
  and and_7 (and_7_out, brgrinst, in_1);
  and and_8 (and_8_out, INSTRUCBUS[2], brRTI);
  and and_9 (and_9_out, ~in_6, notFCBUS);  // AND_Gate
  and and_10 (and_10_out, ~brorjmp, brbrorjmp);  // AND_Gate
  and and_11 (and_11_out, brregdir, ADDRBUS[2]);
  and and_12 (and_12_out, brdone0, in_2);
  and and_13 (and_13_out, brdone15, in_3);
  and and_14 (and_14_out, ~PHASEFFBUS[2], brnotEXEC);  // AND_Gate
  or or_5 (brcnd, and_7_out, and_8_out, and_9_out, and_10_out, and_11_out, and_12_out, and_13_out, and_14_out);
  assign CMEMBUS[0] = ldMAR ? 1'b1 : 1'bz;  // Controlled_Buffer controlled_buffer_1
  assign CMEMBUS[1] = incMAR ? 1'b1 : 1'bz;  // Controlled_Buffer controlled_buffer_2
  assign CMEMBUS[2] = ldMDR ? 1'b1 : 1'bz;  // Controlled_Buffer controlled_buffer_3
  assign CMEMBUS[6] = mpMDR1 ? 1'b1 : 1'bz;  // Controlled_Buffer controlled_buffer_4
  assign CMEMBUS[7] = mpMDR0 ? 1'b1 : 1'bz;  // Controlled_Buffer controlled_buffer_5
  assign CMEMBUS[8] = mpADD ? 1'b1 : 1'bz;  // Controlled_Buffer controlled_buffer_6
  assign CFFBUS[5] = clEXEC ? 1'b1 : 1'bz;  // Controlled_Buffer controlled_buffer_7
  assign CFFBUS[6] = stINTR ? 1'b1 : 1'bz;  // Controlled_Buffer controlled_buffer_8
  assign CREGBUS[0] = ldDWH ? 1'b1 : 1'bz;  // Controlled_Buffer controlled_buffer_9
  assign CREGBUS[1] = ldDWL ? 1'b1 : 1'bz;  // Controlled_Buffer controlled_buffer_10
  assign CREGBUS[2] = ldREG ? 1'b1 : 1'bz;  // Controlled_Buffer controlled_buffer_11
  assign CREGBUS[3] = incREG ? 1'b1 : 1'bz;  // Controlled_Buffer controlled_buffer_12
  assign CREGBUS[8] = wr ? 1'b1 : 1'bz;  // Controlled_Buffer controlled_buffer_13
  assign CREGBUS[9] = mpREG2 ? 1'b1 : 1'bz;  // Controlled_Buffer controlled_buffer_14
  assign CREGBUS[10] = mpREG1 ? 1'b1 : 1'bz;  // Controlled_Buffer controlled_buffer_15
  assign CREGBUS[11] = mpREG0 ? 1'b1 : 1'bz;  // Controlled_Buffer controlled_buffer_16
  assign CREGBUS[12] = decREG ? 1'b1 : 1'bz;  // Controlled_Buffer controlled_buffer_17
  assign CREGBUS[13] = slREG ? 1'b1 : 1'bz;  // Controlled_Buffer controlled_buffer_18
  assign CREGBUS[14] = PGcntrl ? 1'b1 : 1'bz;  // Controlled_Buffer controlled_buffer_19
  assign CREGBUS[15] = ldPG ? 1'b1 : 1'bz;  // Controlled_Buffer controlled_buffer_20
  assign CREGBUS[20] = mpREGIN2 ? 1'b1 : 1'bz;  // Controlled_Buffer controlled_buffer_21
  assign CREGBUS[21] = mpREGIN1 ? 1'b1 : 1'bz;  // Controlled_Buffer controlled_buffer_22
  assign CREGBUS[22] = mpREGIN0 ? 1'b1 : 1'bz;  // Controlled_Buffer controlled_buffer_23
  assign CREGBUS[23] = ldPSWH ? 1'b1 : 1'bz;  // Controlled_Buffer controlled_buffer_24
  assign CREGBUS[24] = ldPSWL ? 1'b1 : 1'bz;  // Controlled_Buffer controlled_buffer_25
  assign CPSW[0] = clPSWST ? 1'b1 : 1'bz;  // Controlled_Buffer controlled_buffer_26
  assign CPSW[1] = ldN ? 1'b1 : 1'bz;  // Controlled_Buffer controlled_buffer_27
  assign CPSW[2] = ldZ ? 1'b1 : 1'bz;  // Controlled_Buffer controlled_buffer_28
  assign CPSW[3] = ldC ? 1'b1 : 1'bz;  // Controlled_Buffer controlled_buffer_29
  assign CPSW[4] = ldV ? 1'b1 : 1'bz;  // Controlled_Buffer controlled_buffer_30
  assign rdMEM = rdMEM_t ? 1'b1 : 1'bz;  // Controlled_Buffer controlled_buffer_31
  assign wrMEM = wrMEM_t ? 1'b1 : 1'bz;  // Controlled_Buffer controlled_buffer_32

  // Other names for the same wires on the sheet: A15__0[15:0] = A; immed = ADDRBUS[0]; memdir = ADDRBUS[1];
  //   regdir = ADDRBUS[2]; memind = ADDRBUS[3]; postincr = ADDRBUS[4]; pcrelpom = ADDRBUS[5]; ALU15__0[15:0] = ALU;
  //   aluC = out_20; B15__0[15:0] = B; CLK = in_5; done0 = in_2; done15 = in_3; FCBUS = in_6; grinst = in_1;
  //   HALT = INSTRUCBUS[0]; RTS = INSTRUCBUS[1]; RTI = INSTRUCBUS[2]; ASL = INSTRUCBUS[3]; ROLC = INSTRUCBUS[4];
  //   PUSHGPR = INSTRUCBUS[5]; POPGPR = INSTRUCBUS[6]; BLSS = INSTRUCBUS[7]; BNCR = INSTRUCBUS[8];
  //   BGRTU = INSTRUCBUS[9]; BNEG = INSTRUCBUS[10]; JLEQ = INSTRUCBUS[11]; LOOPGRE = INSTRUCBUS[12];
  //   JMP = INSTRUCBUS[13]; JSR = INSTRUCBUS[14]; LD = INSTRUCBUS[15]; ST = INSTRUCBUS[16]; SUB = INSTRUCBUS[17];
  //   AND = INSTRUCBUS[18]; NOT = INSTRUCBUS[19]; EXEC = PHASEFFBUS[2]; PSWSTART = PSW[0]; PSWZ = PSW[1];
  //   PSWN = PSW[2]; PSWV = PSW[3]; PSWC = PSW[4]; PSWI = PSW[15]; rst = in_4

  // Notes on the sheet:
  //   Operaciona jedinica
  //   Upravljacka jedinica
endmodule

module INTR (
  input  in_1,
  input  in_2,
  input  in_3,
  input  [3:0] PHASEFFBUS,
  input  [19:0] INSTRUCBUS,
  input  [15:0] PSW,
  input  [3:0] intr,
  output [15:0] ADDIVTP,
  output [1:0] UEXT1__0,
  output inta,
  output [14:0] CMEMBUS,
  output [7:0] CFFBUS,
  output [31:0] CREGBUS,
  output rdMEM,
  output wrMEM
);

  wire and_2_out, and_3_out, and_4_out, brcnd, brnotFCBUS, brnotINTR, brnotprekid, bruncnd, clINTR, decREG,
       incMAR, ldDWH, ldDWL, ldMAR, ldMDR, ldREG, mpMAR2, mpMDR0, mpMDR1, mpMDR2, mpREG0, mpREGIN1, or_2_out,
       prekid, rdMEM_t, reg8_inc_ld_1_p4, reg8_inc_ld_1_p5, stFETCH, wr, wrMEM_t;
  wire [2:1] DISP;
  wire [7:0] reg8_inc_ld_1_p3;
  wire [15:0] IVTP;
  wire [31:19] rom8x32_1_out_3;

  // REG16_LD reg16_ld_1: pin names not known; wires that end beside it: in_2, {16{1'b0}}, IVTP, in_1
  and and_1 (prekid, or_2_out, PSW[15], ~INSTRUCBUS[0]);  // AND_Gate
  // REG8_INC_LD reg8_inc_ld_1: pin names not known; wires that end beside it: in_2, rom8x32_1_out_3[31:24], reg8_inc_ld_1_p3, reg8_inc_ld_1_p4, reg8_inc_ld_1_p5
  // DC3_8 dc3_8_1: pin names not known; wires that end beside it: rom8x32_1_out_3[22:20], 1'b1, bruncnd, brnotINTR, brnotprekid, brnotFCBUS
  or or_1 (reg8_inc_ld_1_p4, bruncnd, brcnd);
  not not_1 (reg8_inc_ld_1_p5, reg8_inc_ld_1_p4);
  or or_2 (or_2_out, intr[3], intr[2], intr[1], intr[0]);
  ROM8x32 rom8x32_1 (
    .in_1(reg8_inc_ld_1_p3),
    .out_3({rom8x32_1_out_3, clINTR, stFETCH, mpREGIN1, ldDWH, ldDWL, inta, wr, wrMEM_t, rdMEM_t, mpMDR2, mpMDR1, mpMDR0, ldMDR, incMAR, mpMAR2, ldMAR, decREG, mpREG0, ldREG}),
    .in_2(1'b1));
  // CD4 cd4_1: pin names not known; wires that end beside it: intr[3], intr[2], intr[1], intr[0], 1'b1, UEXT1__0[1], UEXT1__0[0]
  // REG2_LD reg2_ld_1: pin names not known; wires that end beside it: in_2, UEXT1__0, DISP, inta
  // ADD16 add16_1: pin names not known; wires that end beside it: IVTP, ADDIVTP, {{13{1'b0}}, DISP, 1'b0}, 1'b0
  and and_2 (and_2_out, ~prekid, brnotprekid);  // AND_Gate
  and and_3 (and_3_out, ~PHASEFFBUS[3], brnotINTR);  // AND_Gate
  and and_4 (and_4_out, ~in_3, brnotFCBUS);  // AND_Gate
  or or_3 (brcnd, and_2_out, and_3_out, and_4_out);
  assign CMEMBUS[0] = ldMAR ? 1'b1 : 1'bz;  // Controlled_Buffer controlled_buffer_1
  assign CMEMBUS[1] = incMAR ? 1'b1 : 1'bz;  // Controlled_Buffer controlled_buffer_2
  assign CMEMBUS[2] = ldMDR ? 1'b1 : 1'bz;  // Controlled_Buffer controlled_buffer_3
  assign CMEMBUS[5] = mpMDR2 ? 1'b1 : 1'bz;  // Controlled_Buffer controlled_buffer_4
  assign CMEMBUS[6] = mpMDR1 ? 1'b1 : 1'bz;  // Controlled_Buffer controlled_buffer_5
  assign CMEMBUS[7] = mpMDR0 ? 1'b1 : 1'bz;  // Controlled_Buffer controlled_buffer_6
  assign CMEMBUS[9] = mpMAR2 ? 1'b1 : 1'bz;  // Controlled_Buffer controlled_buffer_7
  assign CFFBUS[0] = stFETCH ? 1'b1 : 1'bz;  // Controlled_Buffer controlled_buffer_8
  assign CFFBUS[7] = clINTR ? 1'b1 : 1'bz;  // Controlled_Buffer controlled_buffer_9
  assign CREGBUS[0] = ldDWH ? 1'b1 : 1'bz;  // Controlled_Buffer controlled_buffer_10
  assign CREGBUS[1] = ldDWL ? 1'b1 : 1'bz;  // Controlled_Buffer controlled_buffer_11
  assign CREGBUS[2] = ldREG ? 1'b1 : 1'bz;  // Controlled_Buffer controlled_buffer_12
  assign CREGBUS[8] = wr ? 1'b1 : 1'bz;  // Controlled_Buffer controlled_buffer_13
  assign CREGBUS[11] = mpREG0 ? 1'b1 : 1'bz;  // Controlled_Buffer controlled_buffer_14
  assign CREGBUS[12] = decREG ? 1'b1 : 1'bz;  // Controlled_Buffer controlled_buffer_15
  assign CREGBUS[21] = mpREGIN1 ? 1'b1 : 1'bz;  // Controlled_Buffer controlled_buffer_16
  assign rdMEM = rdMEM_t ? 1'b1 : 1'bz;  // Controlled_Buffer controlled_buffer_17
  assign wrMEM = wrMEM_t ? 1'b1 : 1'bz;  // Controlled_Buffer controlled_buffer_18

  // Other names for the same wires on the sheet: ldBR = inta; ADDIVTP15__0[15:0] = ADDIVTP; CLK = in_2; FCBUS = in_3;
  //   HALT = INSTRUCBUS[0]; intr3__0[3:0] = intr; INTR_t = PHASEFFBUS[3]; PSWI = PSW[15]; rst = in_1

  // Notes on the sheet:
  //   Operaciona jedinica
  //   Upravljacka jedinica
endmodule

module RAM (
  input  [15:0] in_1,
  input  in_2,
  input  [7:0] in_3,
  input  in_4,
  input  in_5,
  input  in_6,
  output [7:0] out_7,
  output out_8
);

  wire and_1_out, and_2_out, CNT0, LDCNT, not_1_out, notCNT0, or_1_out, reg4_ld_sl_sr_1_p6, rsff_2_p4,
       rsff_2_p5, rsff_3_p4, sl;
  wire [3:0] CNT, LFSR;

  // RSFF rsff_1: pin names not known; wires that end beside it: 1'b0, in_2, in_6, sl
  or or_1 (or_1_out, in_4, in_5);
  // REG4_LD_SL_SR reg4_ld_sl_sr_1: pin names not known; wires that end beside it: 1'b0, 1'b0, in_2, 4'b1111, LFSR, reg4_ld_sl_sr_1_p6, sl, in_6
  // RisingEdge risingedge_1: pin names not known; wires that end beside it: or_1_out, in_2, LDCNT
  // MEM64Kx8 mem64kx8_1: pin names not known; wires that end beside it: in_1, 1'b1, in_2, in_3, out_7, in_4
  xor xor_1 (reg4_ld_sl_sr_1_p6, LFSR[2], LFSR[3]);
  and and_1 (and_1_out, CNT0, not_1_out);
  not not_1 (not_1_out, LDCNT);
  // RSFF rsff_2: pin names not known; wires that end beside it: and_1_out, in_2, LDCNT, rsff_2_p4, rsff_2_p5
  not not_2 (rsff_2_p4, in_6);
  and and_2 (and_2_out, rsff_2_p5, CNT0);
  // REG4m_DEC_LD reg4m_dec_ld_1: pin names not known; wires that end beside it: in_2, LFSR, CNT, LDCNT, notCNT0, notCNT0
  or or_2 (notCNT0, CNT[0], CNT[1], CNT[2], CNT[3]);
  // RSFF rsff_3: pin names not known; wires that end beside it: out_8, in_2, and_2_out, rsff_3_p4, out_8
  not not_3 (rsff_3_p4, in_6);
  not not_4 (CNT0, notCNT0);

  // Other names for the same wires on the sheet: ADR[15:0] = in_1; CLK = in_2; DIN[7:0] = in_3; DOUT[7:0] = out_7;
  //   fc = out_8; RDMEM = in_5; rst = in_6; WRMEM = in_4

  // Notes on the sheet:
  //   Random broj predstavlja vreme pristupa memoriji
  //   Brojac za generisanje random broja 
  //   Jedinica za generisanje function complete (fc) signala
  //   Brojac za dekrementiranje random broja
endmodule
